# Fritzing sketch fritzing-sketch (saved by Fritzing 0.9.3b)

parts:
  U1 = NodeMCU V1.0
  R1 = Resistor [tolerance=±5% resistance=220 package="0603 [SMD]"]
  C1 = Capacitor [package=cap-pth-small2]
  DHT1 = DHT22 Humidity and Temperature Sensor

nets:
  3V3: U1.3V3, R1.Pin_1, C1.1, DHT1.VDD
  GND: U1.GND, DHT1.GND
  N1: U1.D7, R1.Pin_0, C1.2, DHT1.NULL

custom parts:
  NodeMCU V1.0: ESP8266 based NodeMCU
